// Digital circuit somador.dig as structural Verilog
module somador (
  input  in_1,
  input  in_2,
  input  in_5,
  input  in_6,
  input  in_8,
  input  in_9,
  input  in_11,
  input  in_12,
  input  in_14,
  input  in_15,
  input  in_17,
  input  in_18,
  input  in_20,
  input  in_21,
  input  in_23,
  input  in_24,
  input  in_28,
  input  in_29,
  input  in_31,
  output out_3,
  output out_4,
  output out_7,
  output out_10,
  output out_13,
  output out_16,
  output out_19,
  output out_22,
  output out_25,
  output out_26,
  output out_27,
  output out_30
);

  wire add_2_c_o, add_3_c_o, add_4_c_o, and_1_out, and_2_out, and_3_out, and_4_out, and_5_out, and_6_out,
       and_7_out, or_1_out, or_2_out, or_4_out, or_5_out, xor_1_out, xor_4_out, xor_6_out, xor_8_out;

  xor xor_1 (xor_1_out, in_28, in_29);
  and and_1 (and_1_out, in_28, in_29);
  xor xor_2 (out_30, xor_1_out, 1'b0);
  and and_2 (and_2_out, ~in_1, in_2);  // And
  and and_3 (and_3_out, in_1, ~in_2);  // And
  and and_4 (and_4_out, in_1, in_2);
  or or_1 (or_1_out, and_1_out, 1'b0);
  Add add_1 (.a(in_23), .b(in_24), .c_i(add_2_c_o), .s(out_25), .c_o(out_26));
  or or_2 (or_2_out, and_2_out, and_3_out);
  Add add_2 (.a(in_20), .b(in_21), .c_i(add_3_c_o), .s(out_22), .c_o(add_2_c_o));
  or or_3 (out_4, and_4_out, in_31);
  xor xor_3 (out_3, or_2_out, in_31);
  xor xor_4 (xor_4_out, in_5, in_6);
  and and_5 (and_5_out, in_5, in_6);
  Add add_3 (.a(in_17), .b(in_18), .c_i(add_4_c_o), .s(out_19), .c_o(add_3_c_o));
  xor xor_5 (out_7, xor_4_out, or_1_out);
  or or_4 (or_4_out, and_5_out, or_1_out);
  Add add_4 (.a(in_14), .b(in_15), .c_i(1'b0), .s(out_16), .c_o(add_4_c_o));
  xor xor_6 (xor_6_out, in_8, in_9);
  and and_6 (and_6_out, in_8, in_9);
  xor xor_7 (out_10, xor_6_out, or_4_out);
  or or_5 (or_5_out, and_6_out, or_4_out);
  xor xor_8 (xor_8_out, in_11, in_12);
  and and_7 (and_7_out, in_11, in_12);
  xor xor_9 (out_13, xor_8_out, or_5_out);
  or or_6 (out_27, and_7_out, or_5_out);
endmodule
